// Logisim project Ula1bit.circ as structural Verilog: 3 circuits, main circuit main
module main (
  input  Te,
  input  A,
  input  B,
  input  [2:0] Seletores,
  output out_5,
  output out_6,
  output \Saída 
);

  wire and_out, not_1_out, not_2_out, not_3_out, or_out, somador_1_s, subtrator_1_s, xor_out;

  and \and  (and_out, A, B);
  not not_1 (not_1_out, and_out);
  or \or  (or_out, A, B);
  not not_2 (not_2_out, or_out);
  xor \xor  (xor_out, A, B);
  not not_3 (not_3_out, xor_out);
  Multiplexer #(.select(3), .enable("false")) multiplexer_1 (
    .in0(and_out), .in1(not_1_out), .in2(or_out), .in3(not_2_out), .in4(xor_out), .in5(not_3_out),
    .in6(somador_1_s), .in7(subtrator_1_s), .out(\Saída ), .sel(Seletores));
  somador somador_1 (.A(A), .B(B), .Te(Te), .S(somador_1_s), .Ts(out_5));
  subtrator subtrator_1 (.A(A), .B(B), .Te(Te), .S(subtrator_1_s), .Ts(out_6));

  // Notes on the sheet:
  //   ENTRADAS
  //   AND
  //   NAND
  //   OR
  //   NOR
  //   XOR
  //   XNOR
endmodule

// SOMADOR
module somador (
  input  A,
  input  B,
  input  Te,
  output S,
  output Ts
);

  wire and_1_out, and_2_out, and_3_out, xor_1_out;

  xor xor_1 (xor_1_out, A, B);
  and and_1 (and_1_out, A, B);
  and and_2 (and_2_out, Te, B);
  and and_3 (and_3_out, Te, A);
  xor xor_2 (S, xor_1_out, Te);
  or or_1 (Ts, and_1_out, and_2_out, and_3_out);
endmodule

// SUBTRATOR
module subtrator (
  input  A,
  input  B,
  input  Te,
  output S,
  output Ts
);

  wire and_1_out, and_2_out, and_3_out, not_1_out, xor_1_out;

  not not_1 (not_1_out, A);
  xor xor_1 (xor_1_out, A, B);
  and and_1 (and_1_out, B, Te);
  and and_2 (and_2_out, Te, not_1_out);
  and and_3 (and_3_out, B, not_1_out);
  xor xor_2 (S, xor_1_out, Te);
  or or_1 (Ts, and_1_out, and_2_out, and_3_out);
endmodule
