// Logisim project IncreDecre.circ as structural Verilog: 4 circuits, main circuit incremento
module incremento (
  input  E3,
  input  E2,
  input  E1,
  input  E0,
  output S4,
  output S3,
  output S2,
  output S1,
  output S0
);

  wire meiosomador_2_cout, meiosomador_3_cout, meiosomador_4_cout;

  meioSomador meiosomador_1 (.A(E3), .B(meiosomador_2_cout), .S(S3), .Cout(S4));
  meioSomador meiosomador_2 (.A(E2), .B(meiosomador_3_cout), .S(S2), .Cout(meiosomador_2_cout));
  meioSomador meiosomador_3 (.A(E1), .B(meiosomador_4_cout), .S(S1), .Cout(meiosomador_3_cout));
  meioSomador meiosomador_4 (.A(E0), .B(1'b1), .S(S0), .Cout(meiosomador_4_cout));
endmodule

module decremento (
  input  E3,
  input  E2,
  input  E1,
  input  E0,
  output S4,
  output S3,
  output S2,
  output S1,
  output S0
);

  wire meiosubtrator_2_cout, meiosubtrator_3_cout, meiosubtrator_4_cout;

  meioSubtrator meiosubtrator_1 (.A(E3), .B(meiosubtrator_2_cout), .S(S3), .Cout(S4));
  meioSubtrator meiosubtrator_2 (.A(E2), .B(meiosubtrator_3_cout), .S(S2), .Cout(meiosubtrator_2_cout));
  meioSubtrator meiosubtrator_3 (.A(E1), .B(meiosubtrator_4_cout), .S(S1), .Cout(meiosubtrator_3_cout));
  meioSubtrator meiosubtrator_4 (.A(E0), .B(1'b1), .S(S0), .Cout(meiosubtrator_4_cout));
endmodule

// MS
module meioSomador (
  input  A,
  input  B,
  output S,
  output Cout
);

  xor xor_1 (S, A, B);
  and and_1 (Cout, A, B);
endmodule

// Msb
module meioSubtrator (
  input  A,
  input  B,
  output S,
  output Cout
);

  wire not_1_out;

  not not_1 (not_1_out, A);
  xor xor_1 (S, A, B);
  and and_1 (Cout, not_1_out, B);
endmodule
