// Logisim project Ula4bits.circ as structural Verilog: 3 circuits, main circuit Ula
module Ula (
  input  A3,
  input  A2,
  input  A1,
  input  A0,
  input  B3,
  input  B2,
  input  B1,
  input  B0,
  input  [1:0] Seletor,
  output [4:0] \Saída 
);

  wire display1saida_1_abd, display1saida_1_c, display1saida_1_e, display1saida_1_f, display1saida_1_g,
       display2saida_1_a, display2saida_1_b, display2saida_1_c, display2saida_1_d, display2saida_1_e,
       display2saida_1_f, display2saida_1_g, n1display_1_s, n1display_2_s, n2display_1_a, n2display_1_b,
       n2display_1_c, n2display_1_e, n2display_1_f, n2display_1_g, n2display_1_out_8, n2display_2_a,
       n2display_2_b, n2display_2_c, n2display_2_e, n2display_2_f, n2display_2_g, n2display_2_out_8,
       not_1_out, not_2_out, somador_2_cout, somador_3_cout, Somador_cout, subtrator_2_ts, subtrator_3_ts,
       Subtrator_ts;
  wire [4:0] Decremento_s0, Incremento_s0, Somador_s, Subtrator_s;

  somador Somador (.S1(B0), .S2(A0), .Cin(1'b0), .S(Somador_s[0]), .Cout(Somador_cout));
  somador somador_2 (.S1(B1), .S2(A1), .Cin(Somador_cout), .S(Somador_s[1]), .Cout(somador_2_cout));
  somador somador_3 (.S1(B2), .S2(A2), .Cin(somador_2_cout), .S(Somador_s[2]), .Cout(somador_3_cout));
  somador somador_4 (.S1(B3), .S2(A3), .Cin(somador_3_cout), .S(Somador_s[3]), .Cout(Somador_s[4]));
  subtrator Subtrator (.A(A0), .B(B0), .Te(1'b0), .S(Subtrator_s[0]), .Ts(Subtrator_ts));
  subtrator subtrator_2 (.A(A1), .B(B1), .Te(Subtrator_ts), .S(Subtrator_s[1]), .Ts(subtrator_2_ts));
  subtrator subtrator_3 (.A(A2), .B(B2), .Te(subtrator_2_ts), .S(Subtrator_s[2]), .Ts(subtrator_3_ts));
  subtrator subtrator_4 (.A(A3), .B(B3), .Te(subtrator_3_ts), .S(Subtrator_s[3]), .Ts(Subtrator_s[4]));
  _1Display u_1display_1 (.S3(B3), .S2(B2), .S1(B1), .S(n1display_1_s));
  not not_1 (not_1_out, 1'b1);
  _1Display u_1display_2 (.S3(A3), .S2(A2), .S1(A1), .S(n1display_2_s));
  not not_2 (not_2_out, 1'b1);
  _7_Segment_Display u_7_segment_display_1 (
    .g(not_1_out), .f(1'b1), .a(n1display_1_s), .b(n1display_1_s), .e(1'b1), .d(n1display_1_s),
    .c(n1display_1_s));  // open: dp
  _7_Segment_Display u_7_segment_display_2 (
    .g(not_2_out), .f(1'b1), .a(n1display_2_s), .b(n1display_2_s), .e(1'b1), .d(n1display_2_s),
    .c(n1display_2_s));  // open: dp
  _7_Segment_Display u_7_segment_display_3 (
    .g(n2display_1_g), .f(n2display_1_f), .a(n2display_1_a), .b(n2display_1_b), .e(n2display_1_e),
    .d(n2display_1_out_8), .c(n2display_1_c));  // open: dp
  _7_Segment_Display u_7_segment_display_4 (
    .g(n2display_2_g), .f(n2display_2_f), .a(n2display_2_a), .b(n2display_2_b), .e(n2display_2_e),
    .d(n2display_2_out_8), .c(n2display_2_c));  // open: dp
  _2Display u_2display_1 (
    .S3(B3), .S2(B2), .S1(B1), .S0(B0), .A(n2display_1_a), .B(n2display_1_b), .C(n2display_1_c),
    .out_8(n2display_1_out_8), .E(n2display_1_e), .F(n2display_1_f), .G(n2display_1_g));
  _2Display u_2display_2 (
    .S3(A3), .S2(A2), .S1(A1), .S0(A0), .A(n2display_2_a), .B(n2display_2_b), .C(n2display_2_c),
    .out_8(n2display_2_out_8), .E(n2display_2_e), .F(n2display_2_f), .G(n2display_2_g));
  decremento Decremento (
    .E3(B3), .E2(B2), .E1(B1), .E0(B0), .S4(Decremento_s0[4]), .S3(Decremento_s0[3]), .S2(Decremento_s0[2]),
    .S1(Decremento_s0[1]), .S0(Decremento_s0[0]));
  incremento Incremento (
    .E3(A3), .E2(A2), .E1(A1), .E0(A0), .S4(Incremento_s0[4]), .S3(Incremento_s0[3]), .S2(Incremento_s0[2]),
    .S1(Incremento_s0[1]), .S0(Incremento_s0[0]));
  Multiplexer #(.select(2), .width(5), .enable("false")) multiplexer_1 (
    .in0(Decremento_s0), .in1(Somador_s), .in2(Incremento_s0), .in3(Subtrator_s), .out(\Saída ), .sel(Seletor));
  display1Saida display1saida_1 (
    .S4(\Saída [4]), .S3(\Saída [3]), .S2(\Saída [2]), .S1(\Saída [1]), .S0(\Saída [0]),
    .ABD(display1saida_1_abd), .C(display1saida_1_c), .E(display1saida_1_e), .F(display1saida_1_f),
    .G(display1saida_1_g));
  _7_Segment_Display u_7_segment_display_5 (
    .g(display1saida_1_g), .f(display1saida_1_f), .a(display1saida_1_abd), .b(display1saida_1_abd),
    .e(display1saida_1_e), .d(display1saida_1_abd), .c(display1saida_1_c));  // open: dp
  display2Saida display2saida_1 (
    .S4(\Saída [4]), .S3(\Saída [3]), .S2(\Saída [2]), .S1(\Saída [1]), .S0(\Saída [0]),
    .A(display2saida_1_a), .B(display2saida_1_b), .C(display2saida_1_c), .D(display2saida_1_d),
    .E(display2saida_1_e), .F(display2saida_1_f), .G(display2saida_1_g));
  _7_Segment_Display u_7_segment_display_6 (
    .g(display2saida_1_g), .f(display2saida_1_f), .a(display2saida_1_a), .b(display2saida_1_b),
    .e(display2saida_1_e), .d(display2saida_1_d), .c(display2saida_1_c));  // open: dp

  // Notes on the sheet:
  //   Cout
  //   Displays entradas B
  //   Displays entrada A
  //   00 - decremento
  //   01 - somador
  //   10 -incremento
  //   11 - subtrator
  //   Displays Saídas
endmodule

module somador (
  input  S1,
  input  S2,
  input  Cin,
  output S,
  output Cout
);

  wire and_1_out, and_2_out, and_3_out, xor_1_out;

  xor xor_1 (xor_1_out, S1, S2);
  and and_1 (and_1_out, S1, S2);
  and and_2 (and_2_out, Cin, S2);
  and and_3 (and_3_out, Cin, S1);
  xor xor_2 (S, xor_1_out, Cin);
  or or_1 (Cout, and_1_out, and_2_out, and_3_out);
endmodule

module subtrator (
  input  A,
  input  B,
  input  Te,
  output S,
  output Ts
);

  wire and_1_out, and_2_out, and_3_out, not_1_out, xor_1_out;

  not not_1 (not_1_out, A);
  xor xor_1 (xor_1_out, A, B);
  and and_1 (and_1_out, B, Te);
  and and_2 (and_2_out, Te, not_1_out);
  and and_3 (and_3_out, B, not_1_out);
  xor xor_2 (S, xor_1_out, Te);
  or or_1 (Ts, and_1_out, and_2_out, and_3_out);
endmodule
