// Logisim project displayEntrada.circ as structural Verilog: 11 circuits, main circuit main
module _2Display (
  input  S3,
  input  S2,
  input  S1,
  input  S0,
  output A,
  output B,
  output C,
  output out_8,
  output E,
  output F,
  output G
);

  display_a display_a (.A(S3), .B(S2), .C(S1), .D(S0), .A_2(A));
  display_b display_b (.A(S3), .B(S2), .C(S1), .D(S0), .b_2(B));
  display_c display_c (.A(S3), .B(S2), .C(S1), .D(S0), .c_2(C));
  display_d display_d (.A(S3), .B(S2), .C(S1), .D(S0), .d_2(out_8));
  display_e display_e (.A(S3), .B(S2), .C(S1), .D(S0), .e(E));
  display_f display_f (.A(S3), .B(S2), .C(S1), .D(S0), .f(F));
  display_g display_g (.A(S3), .B(S2), .C(S1), .D(S0), .g(G));
endmodule

module _1Display (
  input  S3,
  input  S2,
  input  S1,
  output S
);

  wire and_1_out, not_1_out, not_2_out, not_3_out;

  not not_1 (not_1_out, S3);
  not not_2 (not_2_out, S2);
  not not_3 (not_3_out, S1);
  and and_1 (and_1_out, not_2_out, not_3_out);
  or or_1 (S, not_1_out, and_1_out);
endmodule

module main (
  input  S3,
  input  S2,
  input  S1,
  input  S0
);

  wire display_1_s, display_a_a_2, display_b_b_2, display_c_c_2, display_d_d_2, display_e_e, display_f_f,
       display_g_g, not_1_out;

  display_1 display_1 (.in_1(S3), .in_2(S2), .in_3(S1), .S(display_1_s));
  display_a display_a (.A(S3), .B(S2), .C(S1), .D(S0), .A_2(display_a_a_2));
  display_b display_b (.A(S3), .B(S2), .C(S1), .D(S0), .b_2(display_b_b_2));
  display_c display_c (.A(S3), .B(S2), .C(S1), .D(S0), .c_2(display_c_c_2));
  display_d display_d (.A(S3), .B(S2), .C(S1), .D(S0), .d_2(display_d_d_2));
  display_e display_e (.A(S3), .B(S2), .C(S1), .D(S0), .e(display_e_e));
  display_f display_f (.A(S3), .B(S2), .C(S1), .D(S0), .f(display_f_f));
  display_g display_g (.A(S3), .B(S2), .C(S1), .D(S0), .g(display_g_g));
  not not_1 (not_1_out, 1'b1);
  _7_Segment_Display u_7_segment_display_1 (
    .g(not_1_out), .f(1'b1), .a(display_1_s), .b(display_1_s), .e(1'b1), .d(display_1_s), .c(display_1_s));  // open: dp
  _7_Segment_Display u_7_segment_display_2 (
    .g(display_g_g), .f(display_f_f), .a(display_a_a_2), .b(display_b_b_2), .e(display_e_e),
    .d(display_d_d_2), .c(display_c_c_2));  // open: dp
endmodule

module display_a (
  input  A,
  input  B,
  input  C,
  input  D,
  output A_2
);

  wire xnor_1_out, xor_1_out;

  xor xor_1 (xor_1_out, A, C);
  xnor xnor_1 (xnor_1_out, B, D);
  or or_1 (A_2, xor_1_out, xnor_1_out);
endmodule

module display_b (
  input  A,
  input  B,
  input  C,
  input  D,
  output b_2
);

  wire and_1_out, and_2_out, and_3_out, and_4_out, and_5_out, not_1_out, not_2_out, not_3_out, not_4_out;

  not not_1 (not_1_out, A);
  not not_2 (not_2_out, B);
  not not_3 (not_3_out, C);
  not not_4 (not_4_out, D);
  and and_1 (and_1_out, not_3_out, not_4_out);
  and and_2 (and_2_out, A, not_3_out);
  and and_3 (and_3_out, A, not_4_out);
  and and_4 (and_4_out, not_1_out, C, D);
  and and_5 (and_5_out, not_2_out, not_4_out);
  or or_1 (b_2, and_1_out, and_2_out, and_3_out, and_4_out, and_5_out);
endmodule

module display_c (
  input  A,
  input  B,
  input  C,
  input  D,
  output c_2
);

  wire and_1_out, and_2_out, and_3_out, and_4_out, and_5_out, and_6_out, and_7_out, not_1_out, not_2_out,
       not_3_out, not_4_out;

  not not_1 (not_1_out, A);
  not not_2 (not_2_out, B);
  not not_3 (not_3_out, C);
  not not_4 (not_4_out, D);
  and and_1 (and_1_out, not_1_out, B);
  and and_2 (and_2_out, B, D);
  and and_3 (and_3_out, B, C);
  and and_4 (and_4_out, not_2_out, not_3_out, not_4_out);
  and and_5 (and_5_out, A, not_2_out, not_3_out);
  and and_6 (and_6_out, not_1_out, C, D);
  and and_7 (and_7_out, A, C, not_4_out);
  or or_1 (c_2, and_1_out, and_2_out, and_3_out, and_4_out, and_5_out, and_6_out, and_7_out);
endmodule

module display_d (
  input  A,
  input  B,
  input  C,
  input  D,
  output d_2
);

  wire and_1_out, and_2_out, and_3_out, and_4_out, and_5_out, and_6_out, not_1_out, not_2_out, not_3_out,
       not_4_out;

  not not_1 (not_1_out, A);
  not not_2 (not_2_out, B);
  not not_3 (not_3_out, C);
  not not_4 (not_4_out, D);
  and and_1 (and_1_out, not_2_out, not_4_out);
  and and_2 (and_2_out, B, not_3_out, D);
  and and_3 (and_3_out, A, B, D);
  and and_4 (and_4_out, A, not_3_out, not_4_out);
  and and_5 (and_5_out, not_1_out, C, not_4_out);
  and and_6 (and_6_out, not_1_out, not_2_out, C);
  or or_1 (d_2, and_1_out, and_2_out, and_3_out, and_4_out, and_5_out, and_6_out);
endmodule

module display_e (
  input  A,
  input  B,
  input  C,
  input  D,
  output e
);

  wire and_1_out, and_2_out, and_3_out, and_4_out, not_1_out, not_2_out, not_3_out, not_4_out;

  not not_1 (not_1_out, A);
  not not_2 (not_2_out, B);
  not not_3 (not_3_out, C);
  not not_4 (not_4_out, D);
  and and_1 (and_1_out, not_1_out, C, not_4_out);
  and and_2 (and_2_out, A, not_3_out, not_4_out);
  and and_3 (and_3_out, not_1_out, not_2_out, not_3_out);
  and and_4 (and_4_out, A, not_2_out, C);
  or or_1 (e, and_1_out, and_2_out, and_3_out, and_4_out);
endmodule

module display_f (
  input  A,
  input  B,
  input  C,
  input  D,
  output f
);

  wire and_1_out, and_2_out, not_1_out, not_2_out, not_3_out, not_4_out, xnor_1_out;

  not not_1 (not_1_out, A);
  not not_2 (not_2_out, B);
  not not_3 (not_3_out, C);
  not not_4 (not_4_out, D);
  and and_1 (and_1_out, A, not_2_out);
  xnor xnor_1 (xnor_1_out, A, C);
  and and_2 (and_2_out, B, C, not_4_out);
  or or_1 (f, and_1_out, xnor_1_out, and_2_out);
endmodule

module display_g (
  input  A,
  input  B,
  input  C,
  input  D,
  output g
);

  wire and_1_out, and_2_out, and_3_out, and_4_out, and_5_out, not_1_out, not_2_out, not_3_out, not_4_out;

  not not_1 (not_1_out, A);
  not not_2 (not_2_out, B);
  not not_3 (not_3_out, C);
  not not_4 (not_4_out, D);
  and and_1 (and_1_out, A, B);
  and and_2 (and_2_out, B, not_3_out);
  and and_3 (and_3_out, B, not_4_out);
  and and_4 (and_4_out, A, not_3_out);
  and and_5 (and_5_out, not_1_out, not_2_out, C);
  or or_1 (g, and_1_out, and_2_out, and_3_out, and_4_out, and_5_out);
endmodule

module display_1 (
  input  in_1,
  input  in_2,
  input  in_3,
  output S
);

  wire and_1_out, not_1_out, not_2_out, not_3_out;

  not not_1 (not_1_out, in_1);
  not not_2 (not_2_out, in_2);
  not not_3 (not_3_out, in_3);
  and and_1 (and_1_out, not_2_out, not_3_out);
  or or_1 (S, not_1_out, and_1_out);
endmodule
