// Logisim project displaySaida.circ as structural Verilog: 15 circuits, main circuit main
module display1Saida (
  input  S4,
  input  S3,
  input  S2,
  input  S1,
  input  S0,
  output ABD,
  output C,
  output E,
  output F,
  output G
);

  display_a__b_e_d displa_a__b_e_d (.A(S4), .B(S3), .C(S2), .D(S1), .E(S0), .a__b_e_d(ABD));
  display_c display_c (.A(S4), .B(S3), .C(S2), .D(S1), .E(S0), .c_2(C));
  display_e display_e (.A(S4), .B(S3), .C(S2), .D(S1), .E(S0), .e_2(E));
  display_f display_f (.A(S4), .B(S3), .C(S2), .D(S1), .E(S0), .f(F));
  display_g display_g (.A(S4), .B(S3), .C(S2), .D(S1), .E(S0), .g(G));
endmodule

module display2Saida (
  input  S4,
  input  S3,
  input  S2,
  input  S1,
  input  S0,
  output A,
  output B,
  output C,
  output D,
  output E,
  output F,
  output G
);

  display_a___2 display_a___2 (.A(S4), .B(S3), .C(S2), .D(S1), .E(S0), .a_2(A));
  display_b___2 display_b___2 (.A(S4), .B(S3), .C(S2), .D(S1), .E(S0), .b_2(B));
  display_c___2 display_c___2 (.A(S4), .B(S3), .C(S2), .D(S1), .E(S0), .c_2(C));
  display_d___2 display_d___2 (.A(S4), .B(S3), .C(S2), .D(S1), .E(S0), .d_2(D));
  display_e___2 display_e___2 (.A(S4), .B(S3), .C(S2), .D(S1), .E(S0), .e_2(E));
  display_f___2 display_f__2 (.A(S4), .B(S3), .C(S2), .D(S1), .E(S0), .f(F));
  display_g___2 display_g___2 (.A(S4), .B(S3), .C(S2), .D(S1), .E(S0), .g(G));
endmodule

module main (
  input  S4,
  input  S3,
  input  S2,
  input  S1,
  input  S0
);

  wire displa_a__b_e_d_a__b_e_d, display_a___2_a_2, display_b___2_b_2, display_c___2_c_2, display_c_c_2,
       display_d___2_d_2, display_e___2_e_2, display_e_e_2, display_f__2_f, display_f_f, display_g___2_g,
       display_g_g;

  display_a__b_e_d displa_a__b_e_d (.A(S4), .B(S3), .C(S2), .D(S1), .E(S0), .a__b_e_d(displa_a__b_e_d_a__b_e_d));
  display_c display_c (.A(S4), .B(S3), .C(S2), .D(S1), .E(S0), .c_2(display_c_c_2));
  display_e display_e (.A(S4), .B(S3), .C(S2), .D(S1), .E(S0), .e_2(display_e_e_2));
  display_f display_f (.A(S4), .B(S3), .C(S2), .D(S1), .E(S0), .f(display_f_f));
  display_g display_g (.A(S4), .B(S3), .C(S2), .D(S1), .E(S0), .g(display_g_g));
  display_a___2 display_a___2 (.A(S4), .B(S3), .C(S2), .D(S1), .E(S0), .a_2(display_a___2_a_2));
  display_b___2 display_b___2 (.A(S4), .B(S3), .C(S2), .D(S1), .E(S0), .b_2(display_b___2_b_2));
  display_c___2 display_c___2 (.A(S4), .B(S3), .C(S2), .D(S1), .E(S0), .c_2(display_c___2_c_2));
  display_d___2 display_d___2 (.A(S4), .B(S3), .C(S2), .D(S1), .E(S0), .d_2(display_d___2_d_2));
  display_e___2 display_e___2 (.A(S4), .B(S3), .C(S2), .D(S1), .E(S0), .e_2(display_e___2_e_2));
  display_f___2 display_f__2 (.A(S4), .B(S3), .C(S2), .D(S1), .E(S0), .f(display_f__2_f));
  display_g___2 display_g___2 (.A(S4), .B(S3), .C(S2), .D(S1), .E(S0), .g(display_g___2_g));
  _7_Segment_Display u_7_segment_display_1 (
    .g(display_g_g), .f(display_f_f), .a(displa_a__b_e_d_a__b_e_d), .b(displa_a__b_e_d_a__b_e_d),
    .e(display_e_e_2), .d(displa_a__b_e_d_a__b_e_d), .c(display_c_c_2));  // open: dp
  _7_Segment_Display u_7_segment_display_2 (
    .g(display_g___2_g), .f(display_f__2_f), .a(display_a___2_a_2), .b(display_b___2_b_2),
    .e(display_e___2_e_2), .d(display_d___2_d_2), .c(display_c___2_c_2));  // open: dp
endmodule

module display_a__b_e_d (
  input  A,
  input  B,
  input  C,
  input  D,
  input  E,
  output a__b_e_d
);

  wire and_1_out, and_2_out, and_3_out, and_4_out, and_5_out, not_1_out, not_2_out, not_3_out, not_4_out,
       not_5_out;

  not not_1 (not_1_out, A);
  not not_2 (not_2_out, B);
  not not_3 (not_3_out, C);
  not not_4 (not_4_out, D);
  not not_5 (not_5_out, E);
  and and_1 (and_1_out, not_1_out, not_3_out, not_4_out);
  and and_2 (and_2_out, not_1_out, not_2_out);
  and and_3 (and_3_out, not_2_out, C);
  and and_4 (and_4_out, B, not_3_out, not_4_out);
  and and_5 (and_5_out, A, B);
  or or_1 (a__b_e_d, and_1_out, and_2_out, and_3_out, and_4_out, and_5_out);
endmodule

module display_c (
  input  A,
  input  B,
  input  C,
  input  D,
  input  E,
  output c_2
);

  wire and_1_out, and_2_out, and_3_out, not_1_out, not_2_out, not_3_out, not_4_out, not_5_out;

  not not_1 (not_1_out, A);
  not not_2 (not_2_out, B);
  not not_3 (not_3_out, C);
  not not_4 (not_4_out, D);
  not not_5 (not_5_out, E);
  and and_1 (and_1_out, A, B, C, D);
  and and_2 (and_2_out, not_1_out, not_3_out, not_4_out);
  and and_3 (and_3_out, not_1_out, not_2_out);
  or or_1 (c_2, and_1_out, and_2_out, and_3_out);
endmodule

module display_e (
  input  A,
  input  B,
  input  C,
  input  D,
  input  E,
  output e_2
);

  wire not_1_out, not_2_out, not_3_out, not_4_out, not_5_out;

  not not_1 (not_1_out, A);
  not not_2 (not_2_out, B);
  not not_3 (not_3_out, C);
  not not_4 (not_4_out, D);
  not not_5 (not_5_out, E);
  or or_1 (e_2, not_1_out, not_2_out, not_3_out, not_4_out);
endmodule

module display_f (
  input  A,
  input  B,
  input  C,
  input  D,
  input  E,
  output f
);

  wire and_1_out, not_1_out, not_2_out, not_3_out, not_4_out, not_5_out;

  not not_1 (not_1_out, A);
  not not_2 (not_2_out, B);
  not not_3 (not_3_out, C);
  not not_4 (not_4_out, D);
  not not_5 (not_5_out, E);
  and and_1 (and_1_out, not_2_out, not_3_out);
  or or_1 (f, and_1_out, not_1_out);
endmodule

module display_g (
  input  A,
  input  B,
  input  C,
  input  D,
  input  E,
  output g
);

  wire and_1_out, and_2_out, not_1_out, not_2_out, not_3_out, not_4_out, not_5_out;

  not not_1 (not_1_out, A);
  not not_2 (not_2_out, B);
  not not_3 (not_3_out, C);
  not not_4 (not_4_out, D);
  not not_5 (not_5_out, E);
  and and_1 (and_1_out, A, B);
  and and_2 (and_2_out, A, C);
  or or_1 (g, and_1_out, and_2_out);
endmodule

module display_a___2 (
  input  A,
  input  B,
  input  C,
  input  D,
  input  E,
  output a_2
);

  wire and_1_out, and_2_out, and_3_out, and_4_out, and_5_out, and_6_out, and_7_out, and_8_out, and_9_out,
       not_1_out, not_2_out, not_3_out, not_4_out, not_5_out;

  not not_1 (not_1_out, A);
  not not_2 (not_2_out, B);
  not not_3 (not_3_out, C);
  not not_4 (not_4_out, D);
  not not_5 (not_5_out, E);
  and and_1 (and_1_out, not_2_out, not_3_out, not_5_out);
  and and_2 (and_2_out, not_2_out, D);
  and and_3 (and_3_out, not_1_out, C, E);
  and and_4 (and_4_out, not_1_out, not_3_out, not_5_out);
  and and_5 (and_5_out, B, C, not_4_out);
  and and_6 (and_6_out, A, not_3_out, E);
  and and_7 (and_7_out, A, C, not_5_out);
  and and_8 (and_8_out, not_3_out, D, not_5_out);
  and and_9 (and_9_out, B, not_4_out, E);
  or or_1 (a_2, and_1_out, and_2_out, and_3_out, and_4_out, and_5_out, and_6_out, and_7_out, and_8_out, and_9_out);
endmodule

module display_b___2 (
  input  A,
  input  B,
  input  C,
  input  D,
  input  E,
  output b_2
);

  wire and_1_out, and_2_out, and_3_out, and_4_out, and_5_out, and_6_out, and_7_out, and_8_out, and_9_out,
       and_10_out, and_11_out, and_12_out, not_1_out, not_2_out, not_3_out, not_4_out, not_5_out;

  not not_1 (not_1_out, A);
  not not_2 (not_2_out, B);
  not not_3 (not_3_out, C);
  not not_4 (not_4_out, D);
  not not_5 (not_5_out, E);
  and and_1 (and_1_out, not_1_out, not_4_out, not_5_out);
  and and_2 (and_2_out, not_2_out, not_3_out, D);
  and and_3 (and_3_out, not_2_out, D, E);
  and and_4 (and_4_out, not_1_out, B, not_4_out);
  and and_5 (and_5_out, not_1_out, not_3_out, not_5_out);
  and and_6 (and_6_out, B, C, not_5_out);
  and and_7 (and_7_out, A, not_2_out, not_3_out, E);
  and and_8 (and_8_out, C, not_4_out, not_5_out);
  and and_9 (and_9_out, A, C, not_5_out);
  and and_10 (and_10_out, B, not_4_out, not_5_out);
  and and_11 (and_11_out, A, not_3_out, D, E);
  and and_12 (and_12_out, B, C, not_4_out);
  or or_1 (b_2, and_1_out, and_2_out, and_3_out, and_4_out, and_5_out, and_6_out, and_7_out, and_8_out, and_9_out, and_10_out, and_11_out, and_12_out);
endmodule

module display_c___2 (
  input  A,
  input  B,
  input  C,
  input  D,
  input  E,
  output c_2
);

  wire and_1_out, and_2_out, and_3_out, and_4_out, and_5_out, and_6_out, and_7_out, and_8_out, and_9_out,
       not_1_out, not_2_out, not_3_out, not_4_out, not_5_out;

  not not_1 (not_1_out, A);
  not not_2 (not_2_out, B);
  not not_3 (not_3_out, C);
  not not_4 (not_4_out, D);
  not not_5 (not_5_out, E);
  and and_1 (and_1_out, not_3_out, not_4_out, not_5_out);
  and and_2 (and_2_out, not_2_out, D, E);
  and and_3 (and_3_out, not_2_out, not_4_out, not_5_out);
  and and_4 (and_4_out, not_1_out, C, E);
  and and_5 (and_5_out, not_1_out, C, D);
  and and_6 (and_6_out, B, not_4_out, E);
  and and_7 (and_7_out, B, D, not_5_out);
  and and_8 (and_8_out, A, not_3_out);
  and and_9 (and_9_out, A, not_4_out, not_5_out);
  or or_1 (c_2, and_1_out, and_2_out, and_3_out, and_4_out, and_5_out, and_6_out, and_7_out, and_8_out, and_9_out);
endmodule

module display_d___2 (
  input  A,
  input  B,
  input  C,
  input  D,
  input  E,
  output d_2
);

  wire and_1_out, and_2_out, and_3_out, and_4_out, and_5_out, and_6_out, and_7_out, and_8_out, and_9_out,
       and_10_out, and_11_out, not_1_out, not_2_out, not_3_out, not_4_out, not_5_out;

  not not_1 (not_1_out, A);
  not not_2 (not_2_out, B);
  not not_3 (not_3_out, C);
  not not_4 (not_4_out, D);
  not not_5 (not_5_out, E);
  and and_1 (and_1_out, not_2_out, not_3_out, not_5_out);
  and and_2 (and_2_out, not_1_out, not_2_out, not_3_out, D);
  and and_3 (and_3_out, not_1_out, C, not_4_out, E);
  and and_4 (and_4_out, not_2_out, D, not_5_out);
  and and_5 (and_5_out, not_1_out, not_3_out, not_5_out);
  and and_6 (and_6_out, B, C, not_4_out, not_5_out);
  and and_7 (and_7_out, not_1_out, B, C, E);
  and and_8 (and_8_out, A, C, not_5_out);
  and and_9 (and_9_out, A, not_2_out, C, D);
  and and_10 (and_10_out, A, B, not_3_out, not_4_out, E);
  and and_11 (and_11_out, not_3_out, D, not_5_out);
  or or_1 (d_2, and_1_out, and_2_out, and_3_out, and_4_out, and_5_out, and_6_out, and_7_out, and_8_out, and_9_out, and_10_out, and_11_out);
endmodule

module display_e___2 (
  input  A,
  input  B,
  input  C,
  input  D,
  input  E,
  output e_2
);

  wire and_1_out, and_2_out, and_3_out, and_4_out, and_5_out, and_6_out, and_7_out, and_8_out, and_9_out,
       and_10_out, not_1_out, not_2_out, not_3_out, not_4_out, not_5_out;

  not not_1 (not_1_out, A);
  not not_2 (not_2_out, B);
  not not_3 (not_3_out, C);
  not not_4 (not_4_out, D);
  not not_5 (not_5_out, E);
  and and_1 (and_1_out, not_1_out, not_3_out, not_5_out);
  and and_2 (and_2_out, not_1_out, B, not_3_out, D);
  and and_3 (and_3_out, B, C, not_4_out, not_5_out);
  and and_4 (and_4_out, A, B, C, D);
  and and_5 (and_5_out, A, C, not_5_out);
  and and_6 (and_6_out, A, not_2_out, C, not_4_out);
  and and_7 (and_7_out, not_3_out, D, not_5_out);
  and and_8 (and_8_out, not_2_out, not_3_out, not_5_out);
  and and_9 (and_9_out, not_1_out, not_2_out, not_3_out, not_4_out);
  and and_10 (and_10_out, not_2_out, D, not_5_out);
  or or_1 (e_2, and_1_out, and_2_out, and_3_out, and_4_out, and_5_out, and_6_out, and_7_out, and_8_out, and_9_out, and_10_out);
endmodule

module display_f___2 (
  input  A,
  input  B,
  input  C,
  input  D,
  input  E,
  output f
);

  wire and_1_out, and_2_out, and_3_out, and_4_out, and_5_out, and_6_out, and_7_out, and_8_out, and_9_out,
       and_10_out, and_11_out, and_12_out, and_13_out, not_1_out, not_2_out, not_3_out, not_4_out, not_5_out;

  not not_1 (not_1_out, A);
  not not_2 (not_2_out, B);
  not not_3 (not_3_out, C);
  not not_4 (not_4_out, D);
  not not_5 (not_5_out, E);
  and and_1 (and_1_out, not_1_out, B, D);
  and and_2 (and_2_out, A, not_3_out, not_5_out);
  and and_3 (and_3_out, A, not_2_out, not_3_out, D);
  and and_4 (and_4_out, not_2_out, C, not_4_out);
  and and_5 (and_5_out, not_1_out, C, D, not_5_out);
  and and_6 (and_6_out, B, D, not_5_out);
  and and_7 (and_7_out, not_3_out, not_4_out, not_5_out);
  and and_8 (and_8_out, not_1_out, not_3_out, not_4_out);
  and and_9 (and_9_out, not_2_out, not_4_out, not_5_out);
  and and_10 (and_10_out, B, not_3_out, not_4_out);
  and and_11 (and_11_out, A, not_4_out, not_5_out);
  and and_12 (and_12_out, A, C, not_4_out);
  and and_13 (and_13_out, B, C, D);
  or or_1 (f, and_1_out, and_2_out, and_3_out, and_4_out, and_5_out, and_6_out, and_7_out, and_8_out, and_9_out, and_10_out, and_11_out, and_12_out, and_13_out);
endmodule

module display_g___2 (
  input  A,
  input  B,
  input  C,
  input  D,
  input  E,
  output g
);

  wire and_1_out, and_2_out, and_3_out, and_4_out, and_5_out, and_6_out, and_7_out, and_8_out, not_1_out,
       not_2_out, not_3_out, not_4_out, not_5_out;

  not not_1 (not_1_out, A);
  not not_2 (not_2_out, B);
  not not_3 (not_3_out, C);
  not not_4 (not_4_out, D);
  not not_5 (not_5_out, E);
  and and_1 (and_1_out, not_2_out, D, not_5_out);
  and and_2 (and_2_out, A, not_2_out, D);
  and and_3 (and_3_out, not_2_out, not_3_out, D);
  and and_4 (and_4_out, not_1_out, C, not_5_out);
  and and_5 (and_5_out, not_1_out, C, not_4_out);
  and and_6 (and_6_out, not_1_out, B, C);
  and and_7 (and_7_out, A, not_3_out, not_5_out);
  and and_8 (and_8_out, B, not_4_out);
  or or_1 (g, and_1_out, and_2_out, and_3_out, and_4_out, and_5_out, and_6_out, and_7_out, and_8_out);
endmodule
