// Logisim project FraseNoDisplay.circ as structural Verilog: 1 circuit, main circuit Frase
module Frase (
);

  wire clock_1_out, clock_2_out, d_ff_1_qn, d_ff_2_qn, d_ff_3_qn, d_ff_4_qn, d_ff_5_qn, d_ff_6_qn, d_ff_7_qn,
       d_ff_8_qn, Display_2_a_2, Display_2_b_2, Display_2_c_2, Display_2_d_2, Display_2_e, Display_2_f,
       Display_2_g, Display_a_2, Display_b_2, Display_c_2, Display_d_2, Display_e, Display_f, Display_g;
  wire [3:0] d_ff_1_q, d_ff_5_q;

  Clock clock_1 (.out(clock_1_out));
  D_Flip_Flop d_ff_1 (.clk(clock_1_out), .D(d_ff_1_qn), .Q(d_ff_1_q[0]), .Qn(d_ff_1_qn));  // open: preset, en, reset
  D_Flip_Flop d_ff_2 (.clk(d_ff_1_qn), .D(d_ff_2_qn), .Q(d_ff_1_q[1]), .Qn(d_ff_2_qn));  // open: preset, en, reset
  Display Display (
    .A(d_ff_1_q[3]), .B(d_ff_1_q[2]), .C(d_ff_1_q[1]), .D(d_ff_1_q[0]), .A_2(Display_a_2), .B_2(Display_b_2),
    .C_2(Display_c_2), .D_2(Display_d_2), .E(Display_e), .F(Display_f), .G(Display_g));
  D_Flip_Flop d_ff_3 (.clk(d_ff_2_qn), .D(d_ff_3_qn), .Q(d_ff_1_q[2]), .Qn(d_ff_3_qn));  // open: preset, en, reset
  _7_Segment_Display u_7_segment_display_1 (
    .g(Display_g), .f(Display_f), .a(Display_a_2), .b(Display_b_2), .e(Display_e), .d(Display_d_2),
    .c(Display_c_2));  // open: dp
  D_Flip_Flop d_ff_4 (.clk(d_ff_3_qn), .D(d_ff_4_qn), .Q(d_ff_1_q[3]), .Qn(d_ff_4_qn));  // open: preset, en, reset
  Clock clock_2 (.out(clock_2_out));
  D_Flip_Flop d_ff_5 (.clk(clock_2_out), .D(d_ff_5_qn), .Q(d_ff_5_q[0]), .Qn(d_ff_5_qn));  // open: preset, en, reset
  D_Flip_Flop d_ff_6 (.clk(d_ff_5_q[0]), .D(d_ff_6_qn), .Q(d_ff_5_q[1]), .Qn(d_ff_6_qn));  // open: preset, en, reset
  Display Display_2 (
    .A(d_ff_5_q[3]), .B(d_ff_5_q[2]), .C(d_ff_5_q[1]), .D(d_ff_5_q[0]), .A_2(Display_2_a_2),
    .B_2(Display_2_b_2), .C_2(Display_2_c_2), .D_2(Display_2_d_2), .E(Display_2_e), .F(Display_2_f),
    .G(Display_2_g));
  D_Flip_Flop d_ff_7 (.clk(d_ff_5_q[1]), .D(d_ff_7_qn), .Q(d_ff_5_q[2]), .Qn(d_ff_7_qn));  // open: preset, en, reset
  _7_Segment_Display u_7_segment_display_2 (
    .g(Display_2_g), .f(Display_2_f), .a(Display_2_a_2), .b(Display_2_b_2), .e(Display_2_e),
    .d(Display_2_d_2), .c(Display_2_c_2));  // open: dp
  D_Flip_Flop d_ff_8 (.clk(d_ff_5_q[2]), .D(d_ff_8_qn), .Q(d_ff_5_q[3]), .Qn(d_ff_8_qn));  // open: preset, en, reset

  // Notes on the sheet:
  //   CONTADOR CRESCENTE
  //   FRASE: 
  //   - - SUBI NO ONIBUS - -
  //   CONTADOR DECRESCENTE 
endmodule
