// Logisim project contadores.circ as structural Verilog: 2 circuits, main circuit Crescente
module Crescente (
  output S3,
  output S2,
  output S1,
  output S0
);

  wire clock_1_out, d_ff_1_qn, d_ff_2_qn, d_ff_3_qn, d_ff_4_qn;

  Clock clock_1 (.out(clock_1_out));
  D_Flip_Flop d_ff_1 (.clk(clock_1_out), .D(d_ff_1_qn), .Q(S0), .Qn(d_ff_1_qn));  // open: preset, en, reset
  D_Flip_Flop d_ff_2 (.clk(d_ff_1_qn), .D(d_ff_2_qn), .Q(S1), .Qn(d_ff_2_qn));  // open: preset, en, reset
  D_Flip_Flop d_ff_3 (.clk(d_ff_2_qn), .D(d_ff_3_qn), .Q(S2), .Qn(d_ff_3_qn));  // open: preset, en, reset
  D_Flip_Flop d_ff_4 (.clk(d_ff_3_qn), .D(d_ff_4_qn), .Q(S3), .Qn(d_ff_4_qn));  // open: preset, en, reset
endmodule

module Decrescente (
  output out_1,
  output out_2,
  output out_3,
  output out_4
);

  wire clock_1_out;

  Clock clock_1 (.out(clock_1_out));
  J_K_Flip_Flop j_k_ff_1 (.J(1'b1), .clk(clock_1_out), .K(1'b1), .Qn(out_4));  // open: Q, preset, en, reset
  J_K_Flip_Flop j_k_ff_2 (.J(1'b1), .clk(out_4), .K(1'b1), .Qn(out_3));  // open: Q, preset, en, reset
  J_K_Flip_Flop j_k_ff_3 (.J(1'b1), .clk(out_3), .K(1'b1), .Qn(out_2));  // open: Q, preset, en, reset
  J_K_Flip_Flop j_k_ff_4 (.J(1'b1), .clk(out_2), .K(1'b1), .Qn(out_1));  // open: Q, preset, en, reset
endmodule
