// Logisim project display.circ as structural Verilog: 9 circuits, main circuit Display
module Display (
  input  A,
  input  B,
  input  C,
  input  D,
  output A_2,
  output B_2,
  output C_2,
  output D_2,
  output E,
  output F,
  output G
);

  A u_A (.A(A), .B(B), .C(C), .D(D), .A_2(A_2));
  B u_B (.A(A), .B(B), .C(C), .D(D), .B_2(B_2));
  C u_C (.A(A), .B(B), .C(C), .D(D), .C_2(C_2));
  D u_D (.A(A), .B(B), .C(C), .D(D), .D_2(D_2));
  E u_E (.A(A), .B(B), .C(C), .D(D), .E(E));
  F u_F (.A(A), .B(B), .C(C), .D(D), .F(F));
  G u_G (.A(A), .B(B), .C(C), .D(D), .G(G));
endmodule

module A (
  input  A,
  input  B,
  input  C,
  input  D,
  output A_2
);

  wire and_1_out, and_2_out, and_3_out, and_4_out, not_1_out, not_2_out, not_3_out, not_4_out;

  not not_1 (not_1_out, A);
  not not_2 (not_2_out, C);
  not not_3 (not_3_out, B);
  not not_4 (not_4_out, D);
  and and_1 (and_1_out, not_1_out, C, not_4_out);
  and and_2 (and_2_out, A, not_2_out, D);
  and and_3 (and_3_out, A, not_3_out, not_2_out);
  and and_4 (and_4_out, not_1_out, B, C);
  or or_1 (A_2, and_1_out, and_2_out, and_3_out, and_4_out);
endmodule

module B (
  input  A,
  input  B,
  input  C,
  input  D,
  output B_2
);

  wire and_1_out, and_2_out, not_1_out, not_2_out, not_3_out, not_4_out;

  not not_1 (not_1_out, A);
  not not_2 (not_2_out, B);
  not not_3 (not_3_out, D);
  not not_4 (not_4_out, C);
  and and_1 (and_1_out, not_1_out, C, D);
  and and_2 (and_2_out, A, not_4_out, not_3_out);
  or or_1 (B_2, and_1_out, and_2_out);
endmodule

module C (
  input  A,
  input  B,
  input  C,
  input  D,
  output C_2
);

  wire and_1_out, and_2_out, and_3_out, and_4_out, not_1_out, not_2_out, not_3_out, not_4_out;

  not not_1 (not_1_out, A);
  not not_2 (not_2_out, D);
  not not_3 (not_3_out, B);
  not not_4 (not_4_out, C);
  and and_1 (and_1_out, not_1_out, C);
  and and_2 (and_2_out, A, not_4_out);
  and and_3 (and_3_out, B, not_4_out, not_2_out);
  and and_4 (and_4_out, not_3_out, C, D);
  or or_1 (C_2, and_1_out, and_2_out, and_3_out, and_4_out);
endmodule

module D (
  input  A,
  input  B,
  input  C,
  input  D,
  output D_2
);

  wire and_1_out, and_2_out, and_3_out, and_4_out, and_5_out, and_6_out, not_1_out, not_2_out, not_3_out,
       not_4_out;

  not not_1 (not_1_out, A);
  not not_2 (not_2_out, C);
  not not_3 (not_3_out, D);
  not not_4 (not_4_out, B);
  and and_1 (and_1_out, not_1_out, C, D);
  and and_2 (and_2_out, A, not_2_out, not_3_out);
  and and_3 (and_3_out, B, not_2_out, not_3_out);
  and and_4 (and_4_out, not_4_out, C, D);
  and and_5 (and_5_out, not_1_out, not_4_out, C);
  and and_6 (and_6_out, A, B, not_2_out);
  or or_1 (D_2, and_1_out, and_2_out, and_3_out, and_4_out, and_5_out, and_6_out);
endmodule

module E (
  input  A,
  input  B,
  input  C,
  input  D,
  output E
);

  wire and_1_out, and_2_out, not_1_out, not_2_out, not_3_out, not_4_out, xor_1_out;

  not not_1 (not_1_out, A);
  not not_2 (not_2_out, C);
  not not_3 (not_3_out, D);
  not not_4 (not_4_out, B);
  xor xor_1 (xor_1_out, A, B);
  and and_1 (and_1_out, B, not_2_out, not_3_out);
  and and_2 (and_2_out, not_1_out, C, D);
  or or_1 (E, xor_1_out, and_1_out, and_2_out);
endmodule

module F (
  input  A,
  input  B,
  input  C,
  input  D,
  output F
);

  wire and_1_out, and_2_out, not_1_out, not_2_out, not_3_out, not_4_out, xor_1_out;

  not not_1 (not_1_out, A);
  not not_2 (not_2_out, B);
  not not_3 (not_3_out, C);
  not not_4 (not_4_out, D);
  xor xor_1 (xor_1_out, B, C);
  and and_1 (and_1_out, not_1_out, C, D);
  and and_2 (and_2_out, A, not_3_out, not_4_out);
  or or_1 (F, xor_1_out, and_1_out, and_2_out);
endmodule

module G (
  input  A,
  input  B,
  input  C,
  input  D,
  output G
);

  wire and_1_out, and_2_out, not_1_out, not_2_out, not_3_out, not_4_out, xnor_1_out;

  not not_1 (not_1_out, A);
  not not_2 (not_2_out, D);
  not not_3 (not_3_out, B);
  not not_4 (not_4_out, C);
  xnor xnor_1 (xnor_1_out, A, D);
  and and_1 (and_1_out, B, C, not_2_out);
  and and_2 (and_2_out, not_3_out, not_4_out, D);
  or or_1 (G, xnor_1_out, and_1_out, and_2_out);
endmodule

module teste (
  input  A,
  input  B,
  input  C,
  input  D
);

  wire A_a_2, B_b_2, C_c_2, D_d_2, E_e, F_f, G_g;

  A u_A (.A(A), .B(B), .C(C), .D(D), .A_2(A_a_2));
  B u_B (.A(A), .B(B), .C(C), .D(D), .B_2(B_b_2));
  C u_C (.A(A), .B(B), .C(C), .D(D), .C_2(C_c_2));
  D u_D (.A(A), .B(B), .C(C), .D(D), .D_2(D_d_2));
  E E (.A(A), .B(B), .C(C), .D(D), .E(E_e));
  F F (.A(A), .B(B), .C(C), .D(D), .F(F_f));
  G G (.A(A), .B(B), .C(C), .D(D), .G(G_g));
  _7_Segment_Display u_7_segment_display_1 (
    .g(G_g), .f(F_f), .a(A_a_2), .b(B_b_2), .e(E_e), .d(D_d_2), .c(C_c_2));  // open: dp
endmodule
